# Fritzing sketch Med-Minder (saved by Fritzing 0.9.3b)
breadboards: 1

parts:
  Raspberry_Pi_1 = Raspberry Pi 3 [part_number=RPI-3-V1.2]
  J1 = Piezo Speaker
  LED1_connected_to_piezo_buzzer = LED - 5mm [color="Red (633nm)" package="5 mm [THT]"]
  R1 = Resistor [tolerance=±5% resistance=220 package=THT]
  S1 = Pushbutton [package=THT]
  LED2_connected_to_momentary_switch = LED - 5mm [color="Red (633nm)" package="5 mm [THT]"]
  R2 = Resistor [tolerance=±5% resistance=220 package=THT]

nets:
  N1: Raspberry_Pi_1.GPIO24, S1.leg0, R2.Pin_1
  N2: Raspberry_Pi_1.GPIO23, J1.pin2, R1.Pin_0
  N3: Raspberry_Pi_1.GND, LED1_connected_to_piezo_buzzer.cathode, S1.leg1, LED2_connected_to_momentary_switch.cathode
  N4: LED1_connected_to_piezo_buzzer.anode, R1.Pin_1
  N5: LED2_connected_to_momentary_switch.anode, R2.Pin_0
